# Fritzing sketch timer.shield (saved by Fritzing 0.9.3b)
circuit board: 8.82124cm x 5.5cm
breadboards: 1

parts:
  ∞ = Arduino Uno (Rev3)
  BTN_STOP = RCA [package=pth]
  Buzz = Piezo Speaker
  BTN_START = RCA [package=pth]
  220Ω = Resistor [tolerance=±5% resistance=220 package=THT]
  OFF/ON = Toggle Switch [package=THT]
  D3_D2_D1_D0 = female pin header, 4 pins [form="♀ (female)"]
  A5_A4_A3_A2_A1 = female pin header, 5 pins [form="♀ (female)"]
  VIN_GND_5V_3V3 = female pin header, 4 pins [form="♀ (female)"]

nets:
  N1: ∞.A1, A5_A4_A3_A2_A1.pin1
  N2: ∞.A2, A5_A4_A3_A2_A1.pin2
  N3: ∞.A3, A5_A4_A3_A2_A1.pin3
  N4: ∞.A4/SDA, A5_A4_A3_A2_A1.pin4
  N5: ∞.A5/SCL, A5_A4_A3_A2_A1.pin5
  N6: ∞.D11_PWM/MOSI, 220Ω.Pin_1
  N7: ∞.D12/MISO, BTN_STOP.PIN
  N8: ∞.D13/SCK, BTN_START.PIN
  N9: ∞.GND, Buzz.pin2, VIN_GND_5V_3V3.pin3
  N10: ∞.D0/RX, D3_D2_D1_D0.pin1
  N11: ∞.D1/TX, D3_D2_D1_D0.pin2
  N12: ∞.D2, D3_D2_D1_D0.pin3
  N13: ∞.D3_PWM, D3_D2_D1_D0.pin4
  N14: ∞.3V3, VIN_GND_5V_3V3.pin1
  N15: ∞.5V, VIN_GND_5V_3V3.pin2
  N16: ∞.VIN, OFF/ON.COM, VIN_GND_5V_3V3.pin4
  N17: BTN_STOP.SHELL, BTN_START.SHELL
  N18: Buzz.pin1, 220Ω.Pin_0

notes:
  VIN GND
  https://github.com/smokewawelsky/aucts
  Arduino Uno Climbing Timer Shield v1
